# Fritzing sketch sketch_fritzing (saved by Fritzing 0.9.2b)
breadboards: 1

parts:
  Parte1 = HC-SR04 Ultrasonic Rangemeter
  Parte2 = Arduino Uno (Rev3)
  LED1 = smd LED [color="Red (633nm)" package="1206 [SMD]"]
  LED2 = smd LED [color="Yellow (595nm)" package="1206 [SMD]"]  # not connected
  R1 = Resistor [tolerance=±5% resistance=580 package="0402 [SMD]"]  # not connected
  R2 = Resistor [tolerance=±5% resistance=580 package="0402 [SMD]"]  # not connected

nets:
  VCC: Parte1.VCC, Parte2.5V
  N1: Parte1.Trig, Parte2.D13/SCK
  N2: Parte1.Echo, Parte2.D12/MISO
  GND: Parte1.GND, Parte2.GND, LED1.anode
