# Fritzing sketch sketch_fritzing_proximity_lcd (saved by Fritzing 0.9.2b)
breadboards: 1

parts:
  Parte1 = HC-SR04 Ultrasonic Rangemeter
  Parte2 = Arduino Uno (Rev3)
  LED1 = smd LED [color="Red (633nm)" package="1206 [SMD]"]
  LED2 = smd LED [color="Yellow (595nm)" package="1206 [SMD]"]
  R1 = Resistor [tolerance=±5% resistance=580 package="0402 [SMD]"]
  R2 = Resistor [tolerance=±5% resistance=580 package="0402 [SMD]"]
  LCD1 = LCD screen  # not connected

nets:
  VCC: Parte1.VCC, Parte2.5V
  N1: Parte1.Trig, Parte2.D13/SCK
  N2: Parte1.Echo, Parte2.D12/MISO
  GND: Parte1.GND, Parte2.GND
  N3: Parte2.D10_PWM/SS, LED2.anode
  N4: Parte2.D11_PWM/MOSI, LED1.anode
  N5: LED1.cathode, R1.Pin_1
  N6: LED2.cathode, R2.Pin_1
